# Fritzing sketch FR_Master (saved by Fritzing 0.9.3b)
circuit board: 22.7387cm x 13.3404cm
breadboards: 1

parts:
  SD_card_module = MicroSD Card Module
  ZS-042_RTC1 = ZS-042 RTC Module
  Part1 = Bluetooth HC-05 Macho
  Part3 = LSM303 Breakout Board - Tilt-Compensated Compass
  Part4 = Arduino Mega 2560 (Rev3)
  S1 = Pushbutton [package="[THT]"]
  R1 = Resistor [tolerance=±5% resistance=2.2k package="0402 [SMD]"]

nets:
  GND: SD_card_module.GND, ZS-042_RTC1.GND, Part1.GND, Part3.GND, Part4.GND, R1.Pin_1
  VCC: SD_card_module.VCC, ZS-042_RTC1.VCC, Part1.VCC, Part3.VCC, Part4.5V, S1.Pin_1, S1.Pin_2
  N1: SD_card_module.MISO, Part4.D50
  N2: SD_card_module.MOSI, Part4.D51
  N3: SD_card_module.SCK, Part4.D52
  N4: SD_card_module.CS, Part4.D4_PWM
  N5: ZS-042_RTC1.SDA, Part3.SDA_M, Part4.D20/SDA, Part4.SDA
  N6: ZS-042_RTC1.SCL, Part3.SCL_M, Part4.D21/SCL, Part4.SCL
  N7: Part1.TXD, Part4.D5_PWM
  N8: Part1.RXD, Part4.D6_PWM
  N9: Part4.D8_PWM, S1.Pin_3, S1.Pin_4, R1.Pin_0
